# Fritzing sketch simonsays-schematic (saved by Fritzing 0.9.5d)
breadboards: 1

parts:
  Arduino = Arduino Uno (Rev3)
  R1 = Resistor [tolerance=±5% resistance=220 package=THT]
  R2 = Resistor [tolerance=±5% resistance=220 package=THT]
  R3 = Resistor [tolerance=±5% resistance=220 package=THT]
  R4 = Resistor [tolerance=±5% resistance=220 package=THT]
  LED1 = LED - 5mm [color="Red (633nm)" package="5 mm [THT]"]
  LED2 = LED - 5mm [color="Green (570nm)" package="5 mm [THT]"]
  LED3 = LED - 5mm [color="Blue (505nm)" package="5 mm [THT]"]
  LED4 = LED - 5mm [color="Yellow (595nm)" package="5 mm [THT]"]
  S1 = Pushbutton [package="[THT]"]
  S2 = Pushbutton [package="[THT]"]
  S3 = Pushbutton [package="[THT]"]
  Piezo = Piezo Speaker
  S4 = Pushbutton [package="[THT]"]

nets:
  N1: Arduino.D8, R4.Pin_0
  N2: Arduino.D9_PWM, S4.Pin_4
  N3: Arduino.D10_PWM/SS, Piezo.pin1
  N4: Arduino.GND, LED1.cathode, LED2.cathode, LED3.cathode, LED4.cathode, S1.Pin_2, S2.Pin_1, S2.Pin_2, S3.Pin_1, S3.Pin_2, Piezo.pin2, S4.Pin_1, S4.Pin_2
  N5: Arduino.D2, R1.Pin_0
  N6: Arduino.D3_PWM, S1.Pin_3, S1.Pin_4
  N7: Arduino.D4, R2.Pin_0
  N8: Arduino.D5_PWM, S2.Pin_3, S2.Pin_4
  N9: Arduino.D6_PWM, R3.Pin_0
  N10: Arduino.D7, S3.Pin_3, S3.Pin_4
  N11: R1.Pin_1, LED1.anode
  N12: R2.Pin_1, LED2.anode
  N13: R3.Pin_1, LED3.anode
  N14: R4.Pin_1, LED4.anode

notes:
  Simon-Says Game, Lisa Werner
